# Fritzing sketch flipper_1 (saved by Fritzing 0.9.3b)
circuit board: 8.46667cm x 5.64444cm
breadboards: 1

parts:
  Netzanschluss = Screw terminal - 2 pins [package=THT]
  L2 = Inductor [package="400 mil [THT]"]
  Si_T1_4A = Fuse with Handler
  Si_T1_6A = Fuse with Handler
  Si_T0_6A = Fuse with Handler
  Si_T0_6A_2 = Fuse with Handler
  Si_T0_6A_3 = Fuse with Handler
  L1 = Inductor [package="400 mil [THT]"]
  Power_On = SWITCH-SPST-2 [package=switch-spst-vertical]
  Grothe_1912 = TRANSFORMER [package=transformer]
  Grothe_1912_2 = TRANSFORMER [package=transformer]
  Grothe_1932 = TRANSFORMER [package=transformer]
  WA_21003 = TRANSFORMER [package=transformer]
  Power_on = filament bulb
  47nF_/_1000V = Electrolytic Capacitor [package="100 mil [THT, electrolytic]"]
  47nF_/_1000V_2 = Electrolytic Capacitor [package="100 mil [THT, electrolytic]"]
  8Ω_/_1W = Resistor [package=THT]

nets:
  N1: Netzanschluss.pin1, L2.pin_1, 47nF_/_1000V.+
  N2: Netzanschluss.pin2, L1.pin_1, 47nF_/_1000V_2.+
  N3: L2.pin_0, Si_T1_4A.Connector1, 47nF_/_1000V.-
  N4: Si_T1_4A.Connector2, Power_On.P
  N5: Si_T1_6A.Connector1, WA_21003.4
  24V~ (a): Si_T1_6A.Connector2
  N6: Si_T0_6A.Connector1, Grothe_1912_2.3
  8V~ (b): Si_T0_6A.Connector2
  N7: Si_T0_6A_2.Connector1, Grothe_1932.4, Power_on.cathode
  3V~ (a): Si_T0_6A_2.Connector2
  N8: Si_T0_6A_3.Connector1, Grothe_1912.4
  5V~ (b): Si_T0_6A_3.Connector2
  0V (N): L1.pin_0, Grothe_1912.2, Grothe_1912_2.1, Grothe_1932.1, WA_21003.2, 47nF_/_1000V_2.-
  220V~ (L): Power_On.O, Grothe_1912.1, Grothe_1912_2.2, Grothe_1932.2, WA_21003.1
  N.C.: Grothe_1912.3, Grothe_1912_2.4
  24V~ (b)/5V~ (a)/GND: Grothe_1912.5, WA_21003.3
  8V~ (a): Grothe_1912_2.5
  3V~ (b): Grothe_1932.3
  N9: Grothe_1932.5, 8Ω_/_1W.Pin_0
  N10: Power_on.anode, 8Ω_/_1W.Pin_1

notes:
  Flipper, Spannungsversorgung, 1.0
  220V~
  L
  N
  3V~ max. 1A
  5V~ max. 1A
  (bl)
  (rt)
  (gb)
  230V~
  (sw)
  24V~

custom parts:
  Fuse with Handler: Device used to protect against excessive current.
  TRANSFORMER: Small transformers
  TRANSFORMER: Small transformers
  filament bulb: A generic filament bulb.
  Electrolytic Capacitor: electrolytic capacitor
  Resistor: A generic resistor
