# Fritzing sketch flipper_2 (saved by Fritzing 0.9.3b)
breadboards: 1

parts:
  160Ω_/_6W = Resistor [package=THT]
  160Ω_/_6W_2 = Resistor [package=THT]
  Flipperhebel_rechts = AC relay with closing and self-opening contact
  Flipperhebel_links = AC relay with closing and self-opening contact
  Flipperknopf_rechts = Square Pushbutton
  Flipperknopf_links = Square Pushbutton
  Freispiel = Solder Jumper [package=sj_2s-no]
  Gong = bell or gong
  1_Pkt_(blau) = filament bulb
  1_Pkt_(weiß) = filament bulb
  1_Pkt_(weiß)_2 = filament bulb
  1_Pkt_(weiß)_3 = filament bulb
  1_Pkt_(gelb) = filament bulb
  1_Pkt_(rot) = filament bulb
  1_Pkt_(grün) = filament bulb
  6_Ω_/_0_5W = Resistor [package=THT]
  Kugel = SWITCH-SPST-2 [part_number="1 Pkt." package=switch-spst-vertical]
  1_Pkt = SWITCH-SPST-2 [package=switch-spst-vertical]
  1_Pkt_2 = SWITCH-SPST-2 [package=switch-spst-vertical]
  Sensor_Ball_aus = SWITCH-SPST-2 [package=switch-spst-vertical]
  Münzeinwurf = SWITCH-SPST-2 [package=switch-spst-vertical]
  Ballfreigabe = AC relay with closing and self-opening contact
  rot_(li) = filament bulb [part_number="KM 024"]
  grün_(li) = filament bulb [part_number="KM 023"]
  grün_(re) = filament bulb [part_number="KM 023"]
  rot_(re) = filament bulb [part_number="KM 024"]
  weiß_(mt) = filament bulb [part_number="100 Pkt."]
  Slingshot_links_mitte_(a) = AC relay with closing and self-opening contact
  Slingshot_links_mitte_(b) = AC relay with closing and self-opening contact
  Kugel_2 = SWITCH-SPST-2 [package=switch-spst-vertical]
  Slingshot_links_vorne = AC relay with closing and self-opening contact
  Kugel_3 = SWITCH-SPST-2 [package=switch-spst-vertical]
  Slingshot_rechts_hinten = AC relay with closing and self-opening contact
  Kugel_4 = SWITCH-SPST-2 [package=switch-spst-vertical]
  Slingshot_rechts_vorne = AC relay with closing and self-opening contact
  Kugel_5 = SWITCH-SPST-2 [package=switch-spst-vertical]
  Bumper = AC relay with closing and self-opening contact
  Kugel_10_Pkt = SWITCH-SPST-2 [package=switch-spst-vertical]
  1_Pkt_3 = AC relay with closing and self-opening contact
  10_Ω_/_+/-_4% = Resistor [package=THT]
  Kugel_6 = SWITCH-SPST-2 [package=switch-spst-vertical]
  Kugel_7 = SWITCH-SPST-2 [package=switch-spst-vertical]
  Kugel_8 = SWITCH-SPST-2 [package=switch-spst-vertical]
  Kugel_9 = SWITCH-SPST-2 [package=switch-spst-vertical]
  Kugel_10 = SWITCH-SPST-2 [package=switch-spst-vertical]
  10_Pkt = AC relay with closing and self-opening contact
  Taster_100_Pkt = SWITCH-SPST-2 [package=switch-spst-vertical]
  400V = Ceramic Capacitor [part_number=2nF package="100 mil [THT, multilayer]"]
  400V_2 = Ceramic Capacitor [part_number=2nF package="100 mil [THT, multilayer]"]
  400V_3 = Ceramic Capacitor [part_number=2nF package="100 mil [THT, multilayer]"]
  400V_4 = Ceramic Capacitor [part_number=2nF package="100 mil [THT, multilayer]"]
  400V_5 = Ceramic Capacitor [part_number=2nF package="100 mil [THT, multilayer]"]
  400V_6 = Ceramic Capacitor [part_number=100nF package="100 mil [THT, multilayer]"]
  400V_7 = Ceramic Capacitor [part_number=100nF package="100 mil [THT, multilayer]"]
  400V_8 = Ceramic Capacitor [part_number=100nF package="100 mil [THT, multilayer]"]
  400V_9 = Ceramic Capacitor [part_number=100nF package="100 mil [THT, multilayer]"]
  400V_10 = Ceramic Capacitor [part_number=100nF package="100 mil [THT, multilayer]"]
  400V_11 = Ceramic Capacitor [part_number=100nF package="100 mil [THT, multilayer]"]
  +1 = AC relay with closing and self-opening contact
  1er_=_0 = filament bulb
  1er-Steller = SWITCH-SPST-2 [package=switch-spst-vertical]
  10er_=_0 = filament bulb
  10er-Steller = SWITCH-SPST-2 [package=switch-spst-vertical]
  100er_=_1 = filament bulb
  100er-Steller = SWITCH-SPST-2 [package=switch-spst-vertical]

nets:
  220V~ (L): 160Ω_/_6W.Pin_0, 160Ω_/_6W_2.Pin_0, 10_Pkt.switch2, Taster_100_Pkt.P, +1.switch1, 1er-Steller.P, 10er-Steller.P, 100er-Steller.P
  N1: 160Ω_/_6W.Pin_1, Flipperhebel_rechts.coil1
  N2: 160Ω_/_6W_2.Pin_1, Flipperhebel_links.coil1
  N3: Flipperhebel_rechts.coil2, Flipperknopf_rechts.leg1
  N4: Flipperhebel_links.coil2, Flipperknopf_links.leg1
  0V (N): Flipperknopf_rechts.leg0, Flipperknopf_links.leg0
  N5: Freispiel.1, Münzeinwurf.O, Ballfreigabe.coil1
  8V~ (b): Freispiel.2, Sensor_Ball_aus.P, Münzeinwurf.P, 1_Pkt_3.coil1
  8V~ (a): Gong.cathode, Ballfreigabe.coil2, +1.coil2
  N6: Gong.anode, Sensor_Ball_aus.O
  5V~ (a): 1_Pkt_(blau).anode, 1_Pkt_(weiß).anode, 1_Pkt_(weiß)_2.anode, 1_Pkt_(weiß)_3.anode, 1_Pkt_(gelb).anode, 1_Pkt_(rot).anode, 6_Ω_/_0_5W.Pin_0
  N7: 1_Pkt_(blau).cathode, 1_Pkt_(weiß).cathode, 1_Pkt_(weiß)_2.cathode, 1_Pkt_(weiß)_3.cathode, 1_Pkt_(gelb).cathode, 1_Pkt_(rot).cathode, 1_Pkt_(grün).cathode, 1_Pkt_3.switch2
  N8: 1_Pkt_(grün).anode, 6_Ω_/_0_5W.Pin_1
  GND: Kugel.O, 1_Pkt.O, 1_Pkt_2.O, +1.coil1
  N9: Kugel.P, 1_Pkt.P, 1_Pkt_2.P, 1_Pkt_3.coil2
  3V~ (a): rot_(li).cathode, grün_(li).cathode, grün_(re).cathode, rot_(re).cathode, weiß_(mt).cathode
  3V~ (b): rot_(li).anode, grün_(li).anode, grün_(re).anode, rot_(re).anode, weiß_(mt).anode
  24V~ (a): Slingshot_links_mitte_(a).coil1, Slingshot_links_mitte_(b).coil1, Slingshot_links_vorne.coil1, Slingshot_rechts_hinten.coil1, Slingshot_rechts_vorne.coil1, Bumper.coil1, 10_Ω_/_+/-_4%.Pin_0, 10_Pkt.coil2
  N10: Slingshot_links_mitte_(a).coil2, Slingshot_links_mitte_(b).coil2, Kugel_2.P, 400V_6.0, 400V_7.0
  24V~ (b): Kugel_2.O, Kugel_3.O, Kugel_4.O, Kugel_5.O, Kugel_10_Pkt.O, Kugel_6.O, Kugel_7.O, Kugel_8.O, Kugel_9.O, Kugel_10.O, 400V.0, 400V_2.0, 400V_3.0, 400V_4.0, 400V_5.0, 400V_6.1, 400V_7.1, 400V_8.1, 400V_9.1, 400V_10.1, 400V_11.1
  N11: Slingshot_links_vorne.coil2, Kugel_3.P, 400V_8.0
  N12: Slingshot_rechts_hinten.coil2, Kugel_4.P, 400V_9.0
  N13: Slingshot_rechts_vorne.coil2, Kugel_5.P, 400V_10.0
  N14: Bumper.coil2, Kugel_10_Pkt.P, 10_Pkt.coil1, 400V_11.0
  5V~ (b): 1_Pkt_3.switch1
  N15: 10_Ω_/_+/-_4%.Pin_1, Kugel_6.P, Kugel_7.P, Kugel_8.P, Kugel_9.P, Kugel_10.P, 400V.1, 400V_2.1, 400V_3.1, 400V_4.1, 400V_5.1
  +10: 10_Pkt.switch1, 10er-Steller.O
  +100: Taster_100_Pkt.O, 100er-Steller.O
  +1 (a): +1.switch2
  1er = 0: 1er_=_0.cathode
  V~ Steller: 1er_=_0.anode, 10er_=_0.anode, 100er_=_1.anode
  +1 (b): 1er-Steller.O
  10er = 0: 10er_=_0.cathode
  100er = 0: 100er_=_1.cathode

notes:
  Flipper, Spielfeld, 1.0
  Flipperhebel
  (bl)
  (rt)
  Grundbeleuchtung Spielfeld
  (gb)
  (sw)
  Leuchtmelder
  zum Kopfteil
  (ws)
  Slingshots
  Spielablaufsteuerung

custom parts:
  Resistor: A generic resistor
  AC relay with closing and self-opening contact: A generic AC relay with closing contact.
  Square Pushbutton: A generic pushbutton.
  Solder Jumper: Solder Jumper Standard SMD solder jumper. Used to automate production. Two varients : Normally Open and Normally Closed are the same, but have different paste layers. NC will have a large amount of paste and should jumper during reflow.
  bell or gong: A generic bell or gong.
  filament bulb: A generic filament bulb.
  AC relay with closing and self-opening contact: A generic AC relay with closing contact.
  Ceramic Capacitor: multilayer Ceramic Capacitor
