# Fritzing sketch flipper_3 (saved by Fritzing 0.9.3b)
breadboards: 1

parts:
  Lampe_UV = neon lamp
  Lampe_weiß = neon lamp
  Starter_Lampe_UV = Fluorescent Lamp Starter
  Starter_Lampe_weiß = Fluorescent Lamp Starter
  Neon_ein/aus = Press Switch
  Netz-Drossel = Inductor [package="400 mil [THT]"]
  Grothe_1932 = TRANSFORMER [package=transformer]
  6V_/_0_1A = filament bulb
  4V_/_0_3A = filament bulb
  6V_/_0_1A_2 = filament bulb
  6V_/_0_1A_3 = filament bulb
  1er = AC impulse counter with carry and zero
  10er = AC impulse counter with carry and zero
  High_Score = filament bulb
  Si_T0_63A = Fuse with Handler
  100er = AC impulse counter with joker and zero

nets:
  0V (N): Lampe_UV.anode, Starter_Lampe_UV.+, Grothe_1932.1, 1er.coil2, 10er.coil2, 100er.coil2
  N1: Lampe_UV.cathode, Lampe_weiß.anode, Starter_Lampe_UV.-, Starter_Lampe_weiß.+
  N2: Lampe_weiß.cathode, Starter_Lampe_weiß.-, Netz-Drossel.pin_1
  N3: Neon_ein/aus.leg0, Grothe_1932.2, Si_T0_63A.Connector1
  N4: Neon_ein/aus.leg1, Netz-Drossel.pin_0
  N5: Grothe_1932.3, 6V_/_0_1A.cathode, 6V_/_0_1A_2.cathode, 6V_/_0_1A_3.cathode, High_Score.cathode
  V~ Steller: Grothe_1932.4
  N6: Grothe_1932.5, 4V_/_0_3A.anode, 1er.zero1, 10er.zero1, 100er.carry1, 100er.zero1
  N7: 6V_/_0_1A.anode, 4V_/_0_3A.cathode, 6V_/_0_1A_2.anode, 6V_/_0_1A_3.anode
  +1 (a)/+1 (b): 1er.coil1, 1er.carry1
  +10: 1er.carry2, 10er.coil1, 10er.carry1
  1er = 0: 1er.zero2
  +100: 10er.carry2, 100er.coil1
  10er = 0: 10er.zero2
  N8: High_Score.anode, 100er.carry2
  220V~ (L): Si_T0_63A.Connector2
  100er = 0: 100er.zero2

notes:
  Flipper, Kopfteil, 1.0
  (ws)
  (sw)
  5V~ max. 1A
  3V~ max. 1A
  (gr)
  (li)
  Grundbeleuchtung
  Zählwerk Punktestand

custom parts:
  neon lamp: A generic neon lamp.
  Fluorescent Lamp Starter: fluorescent lamp starter
  Press Switch: A generic press switch.
  TRANSFORMER: Small transformers
  filament bulb: A generic filament bulb.
  AC impulse counter with carry and zero: An impulse counter with digits "0" and "9" detector switches.
  Fuse with Handler: Device used to protect against excessive current.
  AC impulse counter with joker and zero: An impulse counter with digits "0" and "*" detector switches.
